# Fritzing sketch Untitled Sketch (saved by Fritzing 0.9.4)
breadboards: 1

parts:
  Part1 = Arduino Mega 2560 (Rev3)
  Chirp!_Soil_Moisture_Sensor1 = Chirp! Soil Moisture Sensor v2.7.3

nets:
  N1: Part1.5V, Chirp!_Soil_Moisture_Sensor1.Pin_1, Chirp!_Soil_Moisture_Sensor1.pin_5
